# Fritzing sketch circuit-levelup (saved by Fritzing 1.0.5)
breadboards: 1

parts:
  R1 = Resistor [tolerance=±5% power=0.25W resistance=10k package=THT]
  CdS_Cell = Photocell (LDR) [power=0.25W dark_resistance_@0.01lx=300kΩ light_resistance_@100lx=400Ω luminance=10lx package=THT]
  Raspberry_Pi_Pico = Raspberry Pi Pico
  Tilt_SW = Tilt Switch [package=THT]
  R2 = Resistor [tolerance=±5% power=0.25W resistance=10k package=THT]
  Push_SW = Pushbutton [package="[THT]"]
  R3 = Resistor [tolerance=±5% power=0.25W resistance=10k package=THT]
  Sounder = Piezo Speaker
  R4 = Resistor [tolerance=±5% power=0.25W resistance=100 package=THT]
  LED1 = LED - 5mm [color="Red (633nm)" current=0.030A package="5 mm [THT]"]
  R5 = Resistor [tolerance=±5% power=0.25W resistance=100 package=THT]

nets:
  3.3V: R1.Pin_0, Raspberry_Pi_Pico.pin_36, R2.Pin_0, R3.Pin_0, R4.Pin_0, R5.Pin_0
  GP 27( A1 ): R1.Pin_1, CdS_Cell.pin_0, Raspberry_Pi_Pico.pin_32
  GND: CdS_Cell.pin_1, Raspberry_Pi_Pico.pin_3, Raspberry_Pi_Pico.pin_8, Raspberry_Pi_Pico.pin_13, Raspberry_Pi_Pico.pin_18, Raspberry_Pi_Pico.pin_23, Raspberry_Pi_Pico.pin_28, Raspberry_Pi_Pico.pin_33, Raspberry_Pi_Pico.pin_38, Tilt_SW.Pin_1, Push_SW.Pin_3, Push_SW.Pin_4
  GP 9: Raspberry_Pi_Pico.pin_12, Push_SW.Pin_1, Push_SW.Pin_2, R3.Pin_1
  GP 10: Raspberry_Pi_Pico.pin_14, Sounder.pin1
  GP 12: Raspberry_Pi_Pico.pin_16, LED1.cathode
  GP 15: Raspberry_Pi_Pico.pin_20, Tilt_SW.Pin_2, R2.Pin_1
  N1: Sounder.pin2, R4.Pin_1
  N2: LED1.anode, R5.Pin_1

custom parts:
  Raspberry Pi Pico: Raspberry Pi Pico. Based around the RP2040 microcontroller the Pico is a low cost microcontroller device bringing Raspberry Pi quality, cost, and easy of use to the microcontroller space. Jan 2021, Split part in to two versions: SMD (this one) and tht. This one is single sided and uses the castellation pads to solder the module to the board (no holes, other than for the USB connector!). The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
