# Fritzing sketch circuit (saved by Fritzing 1.0.5)
breadboards: 1

parts:
  R1 = Resistor [tolerance=±5% power=0.25W resistance=10k package=THT]
  CdS_Cell = Photocell (LDR) [power=0.25W dark_resistance_@0.01lx=300kΩ light_resistance_@100lx=400Ω luminance=10lx package=THT]
  Raspberry_Pi_Pico = Raspberry Pi Pico

nets:
  N1: R1.Pin_0, Raspberry_Pi_Pico.pin_36
  N2: R1.Pin_1, CdS_Cell.pin_0, Raspberry_Pi_Pico.pin_27
  N3: CdS_Cell.pin_1, Raspberry_Pi_Pico.pin_3, Raspberry_Pi_Pico.pin_8, Raspberry_Pi_Pico.pin_13, Raspberry_Pi_Pico.pin_18, Raspberry_Pi_Pico.pin_23, Raspberry_Pi_Pico.pin_28, Raspberry_Pi_Pico.pin_33, Raspberry_Pi_Pico.pin_38

custom parts:
  Raspberry Pi Pico: Raspberry Pi Pico. Based around the RP2040 microcontroller the Pico is a low cost microcontroller device bringing Raspberry Pi quality, cost, and easy of use to the microcontroller space. Jan 2021, Split part in to two versions: SMD (this one) and tht. This one is single sided and uses the castellation pads to solder the module to the board (no holes, other than for the USB connector!). The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
